# Fritzing sketch 01_blinking_led (saved by Fritzing 0.9.4)
breadboards: 1

parts:
  MCU1 = Raspberry Pi Zero
  LED1 = LED - 5mm [color="Red (633nm)" package="5 mm [THT]"]
  LED2 = LED - 5mm [color="Blue (470nm)" package="5 mm [THT]"]
  R1 = Resistor [tolerance=±5% resistance=220 package=THT]
  R2 = Resistor [tolerance=±5% resistance=220 package=THT]

nets:
  N1: MCU1.pin_6, MCU1.pin_8, MCU1.pin_25, R1.Pin_1, R2.Pin_1
  N2: MCU1.pin_10, LED2.anode
  N3: MCU1.pin_12, LED1.anode
  N4: LED1.cathode, R2.Pin_0
  N5: LED2.cathode, R1.Pin_0
