# Fritzing sketch 04_display_1602 (saved by Fritzing 0.9.4)
breadboards: 1

parts:
  MCU1 = Raspberry Pi Zero
  LCD1 = LCD screen
  U1 = POT [package=pot_alpha_rv16af-20]
  U2 = POT [package=pot_alpha_rv16af-20]

nets:
  N1: MCU1.pin_2, MCU1.pin_4, LCD1.VDD, U1.S
  N2: MCU1.pin_6, MCU1.pin_39, LCD1.VSS, LCD1.R/W, LCD1.LED-, U2.E
  N3: MCU1.pin_23, LCD1.DB7
  N4: MCU1.pin_29, LCD1.DB6
  N5: MCU1.pin_31, LCD1.DB5
  N6: MCU1.pin_33, LCD1.DB4
  N7: MCU1.pin_35, LCD1.E
  N8: MCU1.pin_37, LCD1.RS
  N9: LCD1.V0, U2.S
  N10: LCD1.LED+, U1.E
