# Fritzing sketch 06_display_1602_tun_on_off (saved by Fritzing 0.9.4)
breadboards: 1

parts:
  MCU1 = Raspberry Pi Zero
  LCD1 = LCD screen
  U2 = POT [package=pot_alpha_rv16af-20]
  S1 = Pushbutton [package="[SMD]"]

nets:
  N1: MCU1.pin_2, MCU1.pin_4, LCD1.VDD
  N2: MCU1.pin_3, S1.Pin_3, S1.Pin_4
  N3: MCU1.pin_6, MCU1.pin_39, LCD1.VSS, LCD1.R/W, LCD1.LED-, U2.E, S1.Pin_1, S1.Pin_2
  N4: MCU1.pin_21, LCD1.LED+
  N5: MCU1.pin_23, LCD1.DB7
  N6: MCU1.pin_29, LCD1.DB6
  N7: MCU1.pin_31, LCD1.DB5
  N8: MCU1.pin_33, LCD1.DB4
  N9: MCU1.pin_35, LCD1.E
  N10: MCU1.pin_37, LCD1.RS
  N11: LCD1.V0, U2.S
